// Logisim project SAP1.circ as structural Verilog: 5 circuits, main circuit main
module main (
  output [7:0] out_1
);

  wire controller_1_clk;

  ProgramCounter programcounter_1 (.Ep(1'b1), .Cp(1'b0), .CLK(controller_1_clk), .PC(out_1));  // open: CLR_INV
  MAR mar_1 (.WBus(out_1), .Lm(1'b1), .CLK(controller_1_clk), .CE_(1'b1), .out_5(out_1));
  Controller controller_1 (.CLK(controller_1_clk));  // open: out_2
endmodule

module ProgramCounter (
  input  Ep,
  input  Cp,
  input  CLK,
  input  CLR_INV,
  output [7:0] PC
);

  wire not_1_out, not_2_out, not_3_out, not_4_out;
  wire [7:0] c74LS126_q;

  not not_1 (not_1_out, CLK);
  J_K_Flip_Flop c74LS126 (.J(1'b1), .K(1'b1), .clk(not_1_out), .Q(c74LS126_q[0]), .reset(CLR_INV));  // open: Qn, preset
  not not_2 (not_2_out, c74LS126_q[0]);
  J_K_Flip_Flop j_k_ff_1 (.J(1'b1), .K(1'b1), .clk(not_2_out), .Q(c74LS126_q[1]), .reset(CLR_INV));  // open: Qn, preset
  not not_3 (not_3_out, c74LS126_q[1]);
  J_K_Flip_Flop j_k_ff_2 (.J(1'b1), .K(1'b1), .clk(not_3_out), .Q(c74LS126_q[2]), .reset(CLR_INV));  // open: Qn, preset
  not not_4 (not_4_out, c74LS126_q[2]);
  J_K_Flip_Flop j_k_ff_3 (.J(1'b1), .K(1'b1), .clk(not_4_out), .Q(c74LS126_q[3]), .reset(CLR_INV));  // open: Qn, preset
  assign PC = Ep ? c74LS126_q : 8'bz;  // Controlled_Buffer controlled_buffer_1
endmodule

module MAR (
  input  [7:0] WBus,
  input  Lm,
  input  CLK,
  input  CE_,
  output [7:0] out_5
);

  wire multiplexer_1_out, not_1_out, RUN_PROG_sw2, WRITE_sw1;
  wire [3:0] ADDRESS_sw4, c74LS173_q, controlled_buffer_1_out, multiplexer_2_out;
  wire [7:0] DATA_sw8, ram_1_dout;

  // Probe on controlled_buffer_1_out
  assign controlled_buffer_1_out = Lm ? WBus[3:0] : 4'bz;  // Controlled_Buffer controlled_buffer_1
  DipSwitch #(.number(4)) ADDRESS (
    .sw1(ADDRESS_sw4[3]), .sw2(ADDRESS_sw4[2]), .sw3(ADDRESS_sw4[1]), .sw4(ADDRESS_sw4[0]));
  Register #(.width(4)) c74LS173 (.D(controlled_buffer_1_out), .en(1'b1), .clk(CLK), .Q(c74LS173_q), .clr(1'b0));
  DipSwitch #(.number(2)) RUN_PROG (.sw2(RUN_PROG_sw2));  // open: sw1
  // Probe on multiplexer_2_out
  Multiplexer #(.enable("false")) multiplexer_1 (.in0(1'b0), .in1(CE_), .out(multiplexer_1_out), .sel(RUN_PROG_sw2));
  Multiplexer #(.width(4), .enable("false")) multiplexer_2 (
    .in0(ADDRESS_sw4), .in1(c74LS173_q), .out(multiplexer_2_out), .sel(multiplexer_1_out));
  DipSwitch #(.number(2)) WRITE (.sw1(WRITE_sw1));  // open: sw2
  DipSwitch DATA (
    .sw1(DATA_sw8[7]), .sw2(DATA_sw8[6]), .sw3(DATA_sw8[5]), .sw4(DATA_sw8[4]), .sw5(DATA_sw8[3]),
    .sw6(DATA_sw8[2]), .sw7(DATA_sw8[1]), .sw8(DATA_sw8[0]));
  RAM #(.addrWidth(4), .databus("bibus")) ram_1 (
    .addr(multiplexer_2_out), .we(WRITE_sw1), .oe(1'b1), .clk(CLK), .din(DATA_sw8), .dout(ram_1_dout));
  not not_1 (not_1_out, multiplexer_1_out);
  assign out_5 = not_1_out ? ram_1_dout : 8'bz;  // Controlled_Buffer controlled_buffer_2

  // Notes on the sheet:
  //   c74LS819
endmodule

module RingCounter (
  input  CLK,
  input  CLRd,
  output [5:0] out_3
);

  wire j_k_ff_1_q, j_k_ff_2_qn, j_k_ff_3_qn, j_k_ff_4_qn, j_k_ff_5_qn, j_k_ff_6_qn, not_1_out, not_2_out;

  not not_1 (not_1_out, CLK);
  not not_2 (not_2_out, CLRd);
  J_K_Flip_Flop j_k_ff_1 (
    .J(j_k_ff_6_qn), .K(out_3[5]), .clk(not_1_out), .Q(j_k_ff_1_q), .Qn(out_3[0]), .reset(not_2_out));  // open: preset
  J_K_Flip_Flop j_k_ff_2 (
    .J(out_3[0]), .K(j_k_ff_1_q), .clk(not_1_out), .Q(out_3[1]), .Qn(j_k_ff_2_qn), .reset(not_2_out));  // open: preset
  J_K_Flip_Flop j_k_ff_3 (
    .J(out_3[1]), .K(j_k_ff_2_qn), .clk(not_1_out), .Q(out_3[2]), .Qn(j_k_ff_3_qn), .reset(not_2_out));  // open: preset
  J_K_Flip_Flop j_k_ff_4 (
    .J(out_3[2]), .K(j_k_ff_3_qn), .clk(not_1_out), .Q(out_3[3]), .Qn(j_k_ff_4_qn), .reset(not_2_out));  // open: preset
  J_K_Flip_Flop j_k_ff_5 (
    .J(out_3[3]), .K(j_k_ff_4_qn), .clk(not_1_out), .Q(out_3[4]), .Qn(j_k_ff_5_qn), .reset(not_2_out));  // open: preset
  J_K_Flip_Flop j_k_ff_6 (
    .J(out_3[4]), .K(j_k_ff_5_qn), .clk(not_1_out), .Q(out_3[5]), .Qn(j_k_ff_6_qn), .reset(not_2_out));  // open: preset
endmodule

module Controller (
  output CLK,
  output [11:0] out_2
);

  wire [5:0] ringcounter_1_out_3;

  Clock clock_1 (.out(CLK));
  // Probe on ringcounter_1_out_3
  RingCounter ringcounter_1 (.CLK(CLK), .CLRd(1'b1), .out_3(ringcounter_1_out_3));
endmodule
